// Logisim project 6551071077_LAB2_1.circ as structural Verilog: 1 circuit, main circuit main
module main (
  input  A2,
  input  A1,
  input  A0,
  input  EN,
  output Y0,
  output Y1,
  output Y2,
  output Y,
  output Y4,
  output y5,
  output Y6,
  output Y7
);

  wire not_1_out, not_2_out, not_3_out;

  not not_1 (not_1_out, A2);
  not not_2 (not_2_out, A1);
  not not_3 (not_3_out, A0);
  and and_1 (Y0, not_1_out, not_2_out, not_3_out, EN);
  and and_2 (Y1, not_1_out, not_1_out, A0, EN);
  and and_3 (Y2, not_1_out, A1, not_3_out, EN);
  and and_4 (Y, not_1_out, A1, A0, EN);
  and and_5 (Y4, A2, not_2_out, not_3_out, EN);
  and and_6 (y5, A2, not_2_out, A0, EN);
  and and_7 (Y6, A2, A1, not_3_out, EN);
  and and_8 (Y7, A2, A1, A0, EN);
endmodule
