// Logisim project 6551071077_LAB2_2.circ as structural Verilog: 1 circuit, main circuit main
module main (
  input  A,
  input  B,
  input  C,
  output Y
);

  wire and_1_out, \Đỗ_Nhật_Thanh_6551071077_out ;

  xor \u_Đỗ_Nhật_Thanh_6551071077  (\Đỗ_Nhật_Thanh_6551071077_out , A, B);
  and and_1 (and_1_out, \Đỗ_Nhật_Thanh_6551071077_out , C);
endmodule
